// Logisim project cpu.circ as structural Verilog: 1 circuit, main circuit main
module main (
);

  wire button_2_out, clk, d_ff_1_q, d_ff_2_q, d_ff_3_q, d_ff_5_q, demultiplexer_1_out0, demultiplexer_1_out1,
       demultiplexer_1_out2, demultiplexer_1_out3, demultiplexer_1_out4, demultiplexer_1_out5,
       demultiplexer_1_out6, demultiplexer_1_out7, demultiplexer_1_out8, demultiplexer_1_out9,
       demultiplexer_1_out10, demultiplexer_1_out11, demultiplexer_1_out12, demultiplexer_1_out13,
       demultiplexer_1_out14, demultiplexer_1_out15, demultiplexer_2_out0, demultiplexer_2_out1,
       demultiplexer_2_out2, demultiplexer_2_out3, demultiplexer_2_out4, demultiplexer_2_out5,
       demultiplexer_2_out6, demultiplexer_2_out7, demultiplexer_2_out8, demultiplexer_2_out9,
       demultiplexer_2_out10, demultiplexer_2_out11, demultiplexer_2_out12, demultiplexer_2_out13,
       demultiplexer_2_out14, demultiplexer_2_out15, demultiplexer_6_out0, demultiplexer_6_out1,
       demultiplexer_6_out2, exec_op, i_ctrl, i_io, i_math, i_mem, i_reg, or_5_out, or_24_out, reg0w, reg1w,
       reg2w, reg3w, reg4w, reg5w, reg6w, reg7w, reg8w, reg9w, reg10w, reg11w, reg12w, reg13w, reg14w,
       reg15w, regwi1, regwi2, res, xor_1_out, xor_2_out, xor_3_out, xor_4_out;
  wire [3:0] regs1, regs2;
  wire [3:3] not_1_out;
  wire [7:0] demultiplexer_4_out0, demultiplexer_4_out1, demultiplexer_4_out2, demultiplexer_4_out3,
       demultiplexer_4_out4, demultiplexer_4_out5, demultiplexer_4_out6, demultiplexer_4_out7,
       demultiplexer_4_out8, demultiplexer_4_out9, demultiplexer_4_out10, demultiplexer_4_out11,
       demultiplexer_4_out12, demultiplexer_4_out13, demultiplexer_4_out14, demultiplexer_4_out15,
       demultiplexer_5_out0, demultiplexer_5_out1, demultiplexer_5_out2, demultiplexer_5_out3,
       demultiplexer_5_out4, demultiplexer_5_out5, demultiplexer_5_out6, demultiplexer_5_out7,
       demultiplexer_5_out8, demultiplexer_5_out9, demultiplexer_5_out10, demultiplexer_5_out11,
       demultiplexer_5_out12, demultiplexer_5_out13, demultiplexer_5_out14, demultiplexer_5_out15, iop, op0,
       op1, ram_out, reg0d, reg0o, reg1d, reg1o, reg2d, reg2o, reg3d, reg3o, reg4d, reg4o, reg5d, reg5o,
       reg6d, reg6o, reg7d, reg7o, reg8d, reg8o, reg9d, reg9o, reg10d, reg10o, reg11d, reg11o, reg12d,
       reg12o, reg13d, reg13o, reg14d, reg14o, reg15d, reg15o, regdi1, regdi2, regdo1, regdo2;
  wire [15:0] counter_1_q, ram_addr, ram_addr_in_rip;

  Pull_Resistor pull_resistor_1 (.node(clk));
  // Switch switch_1: pin names not known; wires that end beside it: 1'b1, clk
  Button button_1 (.out(res));
  Demultiplexer #(.select(4)) demultiplexer_1 (
    .out0(demultiplexer_1_out0), .out1(demultiplexer_1_out1), .out2(demultiplexer_1_out2),
    .out3(demultiplexer_1_out3), .out4(demultiplexer_1_out4), .out5(demultiplexer_1_out5),
    .out6(demultiplexer_1_out6), .out7(demultiplexer_1_out7), .out8(demultiplexer_1_out8),
    .out9(demultiplexer_1_out9), .out10(demultiplexer_1_out10), .out11(demultiplexer_1_out11),
    .out12(demultiplexer_1_out12), .out13(demultiplexer_1_out13), .out14(demultiplexer_1_out14),
    .out15(demultiplexer_1_out15), .in(regwi1), .sel(regs1));
  Demultiplexer #(.select(4)) demultiplexer_2 (
    .out0(demultiplexer_2_out0), .out1(demultiplexer_2_out1), .out2(demultiplexer_2_out2),
    .out3(demultiplexer_2_out3), .out4(demultiplexer_2_out4), .out5(demultiplexer_2_out5),
    .out6(demultiplexer_2_out6), .out7(demultiplexer_2_out7), .out8(demultiplexer_2_out8),
    .out9(demultiplexer_2_out9), .out10(demultiplexer_2_out10), .out11(demultiplexer_2_out11),
    .out12(demultiplexer_2_out12), .out13(demultiplexer_2_out13), .out14(demultiplexer_2_out14),
    .out15(demultiplexer_2_out15), .in(regwi2), .sel(regs2));
  buf or_1 (regwi1, 1'b0);  // OR_Gate
  buf or_2 (regwi2, 1'b0);  // OR_Gate
  assign regdi1 = {8{1'b0}};  // OR_Gate or_3, 8 bits wide OR_Gate
  assign regdi2 = {8{1'b0}};  // OR_Gate or_4, 8 bits wide OR_Gate
  or or_5 (or_5_out, d_ff_5_q, res);
  Button button_2 (.out(button_2_out));
  xor xor_1 (xor_1_out, button_2_out, clk);
  not not_1 (not_1_out[3], exec_op);
  or or_6 (reg0w, demultiplexer_1_out0, demultiplexer_2_out0);
  or or_7 (reg1w, demultiplexer_1_out1, demultiplexer_2_out1);
  or or_8 (reg2w, demultiplexer_1_out2, demultiplexer_2_out2);
  or or_9 (reg3w, demultiplexer_1_out3, demultiplexer_2_out3);
  or or_10 (reg4w, demultiplexer_1_out4, demultiplexer_2_out4);
  or or_11 (reg5w, demultiplexer_1_out5, demultiplexer_2_out5);
  or or_12 (reg6w, demultiplexer_1_out6, demultiplexer_2_out6);
  or or_13 (reg7w, demultiplexer_1_out7, demultiplexer_2_out7);
  or or_14 (reg8w, demultiplexer_1_out8, demultiplexer_2_out8);
  or or_15 (reg9w, demultiplexer_1_out9, demultiplexer_2_out9);
  or or_16 (reg10w, demultiplexer_1_out10, demultiplexer_2_out10);
  or or_17 (reg11w, demultiplexer_1_out11, demultiplexer_2_out11);
  or or_18 (reg12w, demultiplexer_1_out12, demultiplexer_2_out12);
  or or_19 (reg13w, demultiplexer_1_out13, demultiplexer_2_out13);
  or or_20 (reg14w, demultiplexer_1_out14, demultiplexer_2_out14);
  or or_21 (reg15w, demultiplexer_1_out15, demultiplexer_2_out15);
  assign regs1 = 4'b0000;  // OR_Gate or_22, 4 bits wide OR_Gate
  assign regs2 = 4'b0000;  // OR_Gate or_23, 4 bits wide OR_Gate
  D_Flip_Flop d_ff_1 (.D(1'b1), .clk(clk), .Q(d_ff_1_q), .reset(or_5_out));  // open: Qn, preset
  Demultiplexer #(.select(4)) demultiplexer_3 (
    .out0(i_reg), .out1(i_mem), .out2(i_io), .out3(i_math), .out4(i_ctrl), .in(1'b1),
    .sel({not_1_out[3], iop[6:4]}));  // open: out5, out6, out7, out8, out9, out10, out11, out12, out13, out14, out15
  D_Flip_Flop d_ff_2 (.D(d_ff_1_q), .clk(clk), .Q(d_ff_2_q), .reset(or_5_out));  // open: Qn, preset
  xor xor_2 (xor_2_out, d_ff_1_q, d_ff_2_q);
  Register #(.trigger("falling")) register_1 (.D(ram_out), .en(xor_2_out), .clk(xor_1_out), .Q(iop), .clr(res));
  Demultiplexer #(.select(4), .width(8)) demultiplexer_4 (
    .out0(demultiplexer_4_out0), .out1(demultiplexer_4_out1), .out2(demultiplexer_4_out2),
    .out3(demultiplexer_4_out3), .out4(demultiplexer_4_out4), .out5(demultiplexer_4_out5),
    .out6(demultiplexer_4_out6), .out7(demultiplexer_4_out7), .out8(demultiplexer_4_out8),
    .out9(demultiplexer_4_out9), .out10(demultiplexer_4_out10), .out11(demultiplexer_4_out11),
    .out12(demultiplexer_4_out12), .out13(demultiplexer_4_out13), .out14(demultiplexer_4_out14),
    .out15(demultiplexer_4_out15), .in(regdi1), .sel(regs1));
  Demultiplexer #(.select(4), .width(8)) demultiplexer_5 (
    .out0(demultiplexer_5_out0), .out1(demultiplexer_5_out1), .out2(demultiplexer_5_out2),
    .out3(demultiplexer_5_out3), .out4(demultiplexer_5_out4), .out5(demultiplexer_5_out5),
    .out6(demultiplexer_5_out6), .out7(demultiplexer_5_out7), .out8(demultiplexer_5_out8),
    .out9(demultiplexer_5_out9), .out10(demultiplexer_5_out10), .out11(demultiplexer_5_out11),
    .out12(demultiplexer_5_out12), .out13(demultiplexer_5_out13), .out14(demultiplexer_5_out14),
    .out15(demultiplexer_5_out15), .in(regdi2), .sel(regs2));
  D_Flip_Flop d_ff_3 (.D(d_ff_2_q), .clk(clk), .Q(d_ff_3_q), .reset(or_5_out));  // open: Qn, preset
  xor xor_3 (xor_3_out, d_ff_2_q, d_ff_3_q);
  Register #(.trigger("falling")) register_2 (.D(ram_out), .en(xor_3_out), .clk(xor_1_out), .Q(op0), .clr(res));
  D_Flip_Flop d_ff_4 (.D(d_ff_3_q), .clk(clk), .Q(exec_op), .reset(or_5_out));  // open: Qn, preset
  xor xor_4 (xor_4_out, d_ff_3_q, exec_op);
  or or_24 (or_24_out, xor_2_out, xor_3_out, xor_4_out);
  Register #(.trigger("falling")) register_3 (.D(ram_out), .en(xor_4_out), .clk(xor_1_out), .Q(op1), .clr(res));
  D_Flip_Flop d_ff_5 (.D(exec_op), .clk(clk), .Q(d_ff_5_q), .reset(or_5_out));  // open: Qn, preset
  Counter #(.max('hffff), .width(16)) counter_1 (
    .clr(res), .count(or_24_out), .clk(clk), .Q(counter_1_q));  // open: load, up, D, carry
  assign reg0d = demultiplexer_4_out0 | demultiplexer_5_out0;  // OR_Gate or_25, 8 bits wide
  assign reg1d = demultiplexer_4_out1 | demultiplexer_5_out1;  // OR_Gate or_26, 8 bits wide
  assign reg2d = demultiplexer_4_out2 | demultiplexer_5_out2;  // OR_Gate or_27, 8 bits wide
  assign reg3d = demultiplexer_4_out3 | demultiplexer_5_out3;  // OR_Gate or_28, 8 bits wide
  assign reg4d = demultiplexer_4_out4 | demultiplexer_5_out4;  // OR_Gate or_29, 8 bits wide
  assign reg5d = demultiplexer_4_out5 | demultiplexer_5_out5;  // OR_Gate or_30, 8 bits wide
  assign reg6d = demultiplexer_4_out6 | demultiplexer_5_out6;  // OR_Gate or_31, 8 bits wide
  assign reg7d = demultiplexer_4_out7 | demultiplexer_5_out7;  // OR_Gate or_32, 8 bits wide
  assign reg8d = demultiplexer_4_out8 | demultiplexer_5_out8;  // OR_Gate or_33, 8 bits wide
  assign reg9d = demultiplexer_4_out9 | demultiplexer_5_out9;  // OR_Gate or_34, 8 bits wide
  assign reg10d = demultiplexer_4_out10 | demultiplexer_5_out10;  // OR_Gate or_35, 8 bits wide
  assign reg11d = demultiplexer_4_out11 | demultiplexer_5_out11;  // OR_Gate or_36, 8 bits wide
  assign reg12d = demultiplexer_4_out12 | demultiplexer_5_out12;  // OR_Gate or_37, 8 bits wide
  assign reg13d = demultiplexer_4_out13 | demultiplexer_5_out13;  // OR_Gate or_38, 8 bits wide
  assign reg14d = demultiplexer_4_out14 | demultiplexer_5_out14;  // OR_Gate or_39, 8 bits wide
  assign reg15d = demultiplexer_4_out15 | demultiplexer_5_out15;  // OR_Gate or_40, 8 bits wide
  Multiplexer #(.select(4), .width(8)) multiplexer_1 (
    .in0(reg0o), .in1(reg1o), .in2(reg2o), .in3(reg3o), .in4(reg4o), .in5(reg5o), .in6(reg6o), .in7(reg7o),
    .in8(reg8o), .in9(reg9o), .in10(reg10o), .in11(reg11o), .in12(reg12o), .in13(reg13o), .in14(reg14o),
    .in15(reg15o), .out(regdo1), .sel(regs1));
  assign ram_addr_in_rip = or_24_out ? counter_1_q : 16'bz;  // Controlled_Buffer controlled_buffer_1
  Multiplexer #(.select(4), .width(8)) multiplexer_2 (
    .in0(reg0o), .in1(reg1o), .in2(reg2o), .in3(reg3o), .in4(reg4o), .in5(reg5o), .in6(reg6o), .in7(reg7o),
    .in8(reg8o), .in9(reg9o), .in10(reg10o), .in11(reg11o), .in12(reg12o), .in13(reg13o), .in14(reg14o),
    .in15(reg15o), .out(regdo2), .sel(regs2));
  Register #(.trigger("falling")) register_4 (.D(reg0d), .en(reg0w), .clk(clk), .Q(reg0o), .clr(res));
  Register #(.trigger("falling")) register_5 (.D(reg1d), .en(reg1w), .clk(clk), .Q(reg1o), .clr(res));
  RAM #(.addrWidth(16), .enables("line")) ram_1 (
    .addr(ram_addr), .we(1'b0), .oe(clk), .clk(clk), .din({8{1'b0}}), .dout(ram_out));
  Register #(.trigger("falling")) register_6 (.D(reg2d), .en(reg2w), .clk(clk), .Q(reg2o), .clr(res));
  Register #(.trigger("falling")) register_7 (.D(reg3d), .en(reg3w), .clk(clk), .Q(reg3o), .clr(res));
  Demultiplexer #(.select(3)) demultiplexer_6 (
    .out0(demultiplexer_6_out0), .out1(demultiplexer_6_out1), .out2(demultiplexer_6_out2), .in(1'b1),
    .sel(iop[2:0]));  // open: out3, out4, out5, out6, out7
  Register #(.trigger("falling")) register_8 (.D(reg4d), .en(reg4w), .clk(clk), .Q(reg4o), .clr(res));
  assign ram_addr = ram_addr_in_rip;  // OR_Gate or_41, 16 bits wide OR_Gate
  Register #(.trigger("falling")) register_9 (.D(reg5d), .en(reg5w), .clk(clk), .Q(reg5o), .clr(res));
  Register #(.trigger("falling")) register_10 (.D(reg6d), .en(reg6w), .clk(clk), .Q(reg6o), .clr(res));
  Register #(.trigger("falling")) register_11 (.D(reg7d), .en(reg7w), .clk(clk), .Q(reg7o), .clr(res));
  Register #(.trigger("falling")) register_12 (.D(reg8d), .en(reg8w), .clk(clk), .Q(reg8o), .clr(res));
  Register #(.trigger("falling")) register_13 (.D(reg9d), .en(reg9w), .clk(clk), .Q(reg9o), .clr(res));
  Register #(.trigger("falling")) register_14 (.D(reg8d), .en(reg8w), .clk(clk), .Q(reg8o), .clr(res));
  Register #(.trigger("falling")) register_15 (.D(reg9d), .en(reg9w), .clk(clk), .Q(reg9o), .clr(res));
  Register #(.trigger("falling")) register_16 (.D(reg10d), .en(reg10w), .clk(clk), .Q(reg10o), .clr(res));
  Register #(.trigger("falling")) register_17 (.D(reg11d), .en(reg11w), .clk(clk), .Q(reg11o), .clr(res));
  Register #(.trigger("falling")) register_18 (.D(reg12d), .en(reg12w), .clk(clk), .Q(reg12o), .clr(res));
  Register #(.trigger("falling")) register_19 (.D(reg13d), .en(reg13w), .clk(clk), .Q(reg13o), .clr(res));
  Register #(.trigger("falling")) register_20 (.D(reg14d), .en(reg14w), .clk(clk), .Q(reg14o), .clr(res));
  Register #(.trigger("falling")) register_21 (.D(reg15d), .en(reg15w), .clk(clk), .Q(reg15o), .clr(res));

  // Other names for the same wires on the sheet: iopsub[3:0] = iop[3:0]; op0subhigh[3:0] = op0[7:4];
  //   op0sublow[3:0] = op0[3:0]; regao[15:0] = {reg1o, reg0o}; regbo[15:0] = {reg3o, reg2o}

  // Notes on the sheet:
  //   CLOCK + RESET
  //   REGISTER COMBINATORS
  //   INSTRUCTION SPLITTERS
  //   REGISTER INPUT COMBINERS
  //   REGISTER MUXERS AND DEMUXERS
  //   INSTRUCTION SELECTOR
  //   INSTRUCTION CYCLE + INSTRUCTION LOAD
  //   INSTRUCTION COUNTER
  //   REGISTERS
  //   RAM
  //   REGISTER MANIPULATION
  //   RAM CONTROLS
  //   MOVE
  //   MOVEI
endmodule
